// Digital circuit CPU.dig as structural Verilog
module CPU (
);

  wire A_LD, A_OE, CLK, pc_1_p1, rfile_1_p1, RST;

  // PC pc_1: pin names not known; wires that end beside it: pc_1_p1, pc_1_p1
  // RFILE rfile_1: pin names not known; wires that end beside it: rfile_1_p1, CLK, RST, rfile_1_p1, A_LD, A_OE
  // ALU alu_1: pin names not known; wires that end beside it: rfile_1_p1, rfile_1_p1, A_LD, A_OE, CLK, RST, rfile_1_p1
endmodule
