// Digital circuit CTRLUNIT.dig as structural Verilog
module CTRLUNIT (
  input  [7:0] OPC,
  input  [2:0] microstep,
  input  Z,
  input  C,
  input  N,
  input  V,
  input  I,
  output [15:0] C0_15,
  output [15:0] C16_31,
  output [15:0] C32_47
);

  ROM #(.AddrBits(16), .Bits(16)) _1ROM (.A({I, V, N, C, Z, microstep, OPC}), .sel(1'b1), .D(C0_15));
  ROM #(.AddrBits(16), .Bits(16)) _2ROM (.A({I, V, N, C, Z, microstep, OPC}), .sel(1'b1), .D(C16_31));
  ROM #(.AddrBits(16), .Bits(16)) _3ROM (.A({I, V, N, C, Z, microstep, OPC}), .sel(1'b1), .D(C32_47));

  // Notes on the sheet:
  //   contents of _1ROM (hex, n*v repeats v):
  //   256*dda,8*cfb,8*1c3b,8*3c7b,232*cfb,1536*cfa,256*dda,8*cfb,8*1c3b
  //   ,8*3c7b,232*cfb,1536*cfa,256*dda,8*cfb,8*1c3b,8*3c7b,232*cfb,1536*cfa
  //   ,256*dda,8*cfb,8*1c3b,8*3c7b,232*cfb,1536*cfa,256*dda,8*cfb,8*1c3b
  //   ,8*3c7b,232*cfb,1536*cfa,256*dda,8*cfb,8*1c3b,8*3c7b,232*cfb,1536*cfa
  //   ,256*dda,8*cfb,8*1c3b,8*3c7b,232*cfb,1536*cfa,256*dda,8*cfb,8*1c3b
  //   ,8*3c7b,232*cfb,1536*cfa,256*dda,8*cfb,8*1c3b,8*3c7b,232*cfb,1536*cfa
  //   ,256*dda,8*cfb,8*1c3b,8*3c7b,232*cfb,1536*cfa,256*dda,8*cfb,8*1c3b
  //   ,8*3c7b,232*cfb,1536*cfa,256*dda,8*cfb,8*1c3b,8*3c7b,232*cfb,1536*cfa
  //   ,256*dda,8*cfb,8*1c3b,8*3c7b,232*cfb,1536*cfa,256*dda,8*cfb,8*1c3b
  //   ,8*3c7b,232*cfb,1536*cfa,256*dda,8*cfb,8*1c3b,8*3c7b,232*cfb,1536*cfa
  //   ,256*dda,8*cfb,8*1c3b,8*3c7b,232*cfb,1536*cfa,256*dda,8*cfb,8*1c3b
  //   ,8*3c7b,232*cfb,1536*cfa,256*dda,8*cfb,8*1c3b,8*3c7b,232*cfb,1536*cfa
  //   ,256*dda,8*cfb,8*1c3b,8*3c7b,232*cfb,1536*cfa,256*dda,8*cfb,8*1c3b
  //   ,8*3c7b,232*cfb,1536*cfa,256*dda,8*cfb,8*1c3b,8*3c7b,232*cfb,1536*cfa
  //   ,256*dda,8*cfb,8*1c3b,8*3c7b,232*cfb,1536*cfa,256*dda,8*cfb,8*1c3b
  //   ,8*3c7b,232*cfb,1536*cfa,256*dda,8*cfb,8*1c3b,8*3c7b,232*cfb,1536*cfa
  //   ,256*dda,8*cfb,8*1c3b,8*3c7b,232*cfb,1536*cfa,256*dda,8*cfb,8*1c3b
  //   ,8*3c7b,232*cfb,1536*cfa,256*dda,8*cfb,8*1c3b,8*3c7b,232*cfb,1536*cfa
  //   ,256*dda,8*cfb,8*1c3b,8*3c7b,232*cfb,1536*cfa,256*dda,8*cfb,8*1c3b
  //   ,8*3c7b,232*cfb,1536*cfa,256*dda,8*cfb,8*1c3b,8*3c7b,232*cfb,1536*cfa
  //   ,256*dda,8*cfb,8*1c3b,8*3c7b,232*cfb,1536*cfa,256*dda,8*cfb,8*1c3b
  //   ,8*3c7b,232*cfb,1536*cfa
  //   contents of _2ROM (hex, n*v repeats v):
  //   65536*b6a0
  //   contents of _3ROM (hex, n*v repeats v):
  //   64*280,64*4,1100,1100,1000,1000,1200,1401,110,110,1401,0,1400
  //   ,0,5100,5100,7000,5000,4*0,8*5000,8*5100,0,1001,0,110,110,0,1004
  //   ,110,1004,110,1004,110,1004,110,9400,0,1000,17*0,280,280,0,1201
  //   ,0,1200,4*0,4100,4100,6000,4000,16*0,4100,0,280,280,280,221,0
  //   ,280,0,280,0,280,0,280,0,5200,18*0,124,124,8*0,4*1000,16*0,280
  //   ,0,1004,124,124,211,0,124,0,124,0,124,0,124,20*0,1240,1440,28*0
  //   ,4,0,0,1043,401,1043,0,1043,0,1043,0,1043,0,1043,50*0,4100,0,0,0
  //   ,401,59*0,1000,0,0,0,1043,535*0,64*280,64*4,1100,1100,1000,1000
  //   ,1200,1401,110,110,1401,0,1400,0,5100,5100,7000,5000,4*0,8*5000
  //   ,8*5100,0,1001,0,110,110,0,110,1004,1004,110,1004,110,1004,110
  //   ,9400,0,1000,17*0,280,280,0,1201,0,1200,4*0,4100,4100,6000,4000
  //   ,16*0,4100,0,280,280,280,221,280,0,0,280,0,280,0,280,0,5200,18*0
  //   ,124,124,8*0,4*1000,16*0,280,0,1004,124,124,211,124,0,0,124,0
  //   ,124,0,124,20*0,1240,1440,28*0,4,0,0,1043,401,1043,1043,0,0,1043
  //   ,0,1043,0,1043,50*0,4100,0,0,0,401,59*0,1000,0,0,0,1043,535*0
  //   ,64*280,64*4,1100,1100,1000,1000,1200,1401,110,110,1401,0,1400
  //   ,0,5100,5100,7000,5000,4*0,8*5000,8*5100,0,1001,0,110,110,0,1004
  //   ,110,110,1004,1004,110,1004,110,9400,0,1000,17*0,280,280,0,1201
  //   ,0,1200,4*0,4100,4100,6000,4000,16*0,4100,0,280,280,280,221,0
  //   ,280,280,0,0,280,0,280,0,5200,18*0,124,124,8*0,4*1000,16*0,280
  //   ,0,1004,124,124,211,0,124,124,0,0,124,0,124,20*0,1240,1440,28*0
  //   ,4,0,0,1043,401,1043,0,1043,1043,0,0,1043,0,1043,50*0,4100,0,0,0
  //   ,401,59*0,1000,0,0,0,1043,535*0,64*280,64*4,1100,1100,1000,1000
  //   ,1200,1401,110,110,1401,0,1400,0,5100,5100,7000,5000,4*0,8*5000
  //   ,8*5100,0,1001,0,110,110,0,110,1004,110,1004,1004,110,1004,110
  //   ,9400,0,1000,17*0,280,280,0,1201,0,1200,4*0,4100,4100,6000,4000
  //   ,16*0,4100,0,280,280,280,221,280,0,280,0,0,280,0,280,0,5200,18*0
  //   ,124,124,8*0,4*1000,16*0,280,0,1004,124,124,211,124,0,124,0,0
  //   ,124,0,124,20*0,1240,1440,28*0,4,0,0,1043,401,1043,1043,0,1043
  //   ,0,0,1043,0,1043,50*0,4100,0,0,0,401,59*0,1000,0,0,0,1043,535*0
  //   ,64*280,64*4,1100,1100,1000,1000,1200,1401,110,110,1401,0,1400
  //   ,0,5100,5100,7000,5000,4*0,8*5000,8*5100,0,1001,0,110,110,0,1004
  //   ,110,1004,110,110,1004,1004,110,9400,0,1000,17*0,280,280,0,1201
  //   ,0,1200,4*0,4100,4100,6000,4000,16*0,4100,0,280,280,280,221,0
  //   ,280,0,280,280,0,0,280,0,5200,18*0,124,124,8*0,4*1000,16*0,280
  //   ,0,1004,124,124,211,0,124,0,124,124,0,0,124,20*0,1240,1440,28*0
  //   ,4,0,0,1043,401,1043,0,1043,0,1043,1043,0,0,1043,50*0,4100,0,0,0
  //   ,401,59*0,1000,0,0,0,1043,535*0,64*280,64*4,1100,1100,1000,1000
  //   ,1200,1401,110,110,1401,0,1400,0,5100,5100,7000,5000,4*0,8*5000
  //   ,8*5100,0,1001,0,110,110,0,110,1004,1004,110,110,1004,1004,110
  //   ,9400,0,1000,17*0,280,280,0,1201,0,1200,4*0,4100,4100,6000,4000
  //   ,16*0,4100,0,280,280,280,221,280,0,0,280,280,0,0,280,0,5200,18*0
  //   ,124,124,8*0,4*1000,16*0,280,0,1004,124,124,211,124,0,0,124,124
  //   ,0,0,124,20*0,1240,1440,28*0,4,0,0,1043,401,1043,1043,0,0,1043,1043
  //   ,0,0,1043,50*0,4100,0,0,0,401,59*0,1000,0,0,0,1043,535*0,64*280
  //   ,64*4,1100,1100,1000,1000,1200,1401,110,110,1401,0,1400,0,5100,5100
  //   ,7000,5000,4*0,8*5000,8*5100,0,1001,0,110,110,0,1004,110,110,1004
  //   ,110,1004,1004,110,9400,0,1000,17*0,280,280,0,1201,0,1200,4*0
  //   ,4100,4100,6000,4000,16*0,4100,0,280,280,280,221,0,280,280,0,280
  //   ,0,0,280,0,5200,18*0,124,124,8*0,4*1000,16*0,280,0,1004,124,124
  //   ,211,0,124,124,0,124,0,0,124,20*0,1240,1440,28*0,4,0,0,1043,401
  //   ,1043,0,1043,1043,0,1043,0,0,1043,50*0,4100,0,0,0,401,59*0,1000
  //   ,0,0,0,1043,535*0,64*280,64*4,1100,1100,1000,1000,1200,1401,110,110
  //   ,1401,0,1400,0,5100,5100,7000,5000,4*0,8*5000,8*5100,0,1001,0
  //   ,110,110,0,110,1004,110,1004,110,1004,1004,110,9400,0,1000,17*0
  //   ,280,280,0,1201,0,1200,4*0,4100,4100,6000,4000,16*0,4100,0,280,280,280
  //   ,221,280,0,280,0,280,0,0,280,0,5200,18*0,124,124,8*0,4*1000,16*0
  //   ,280,0,1004,124,124,211,124,0,124,0,124,0,0,124,20*0,1240,1440
  //   ,28*0,4,0,0,1043,401,1043,1043,0,1043,0,1043,0,0,1043,50*0,4100
  //   ,0,0,0,401,59*0,1000,0,0,0,1043,535*0,64*280,64*4,1100,1100,1000,1000
  //   ,1200,1401,110,110,1401,0,1400,0,5100,5100,7000,5000,4*0,8*5000
  //   ,8*5100,0,1001,0,110,110,0,1004,110,1004,110,1004,110,110,1004
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endmodule
